// Logisim project F3.3.1+2_XOR.circ as structural Verilog: 1 circuit, main circuit main
module main (
  input  in_1,
  input  in_2,
  output out_3,
  output out_4,
  output out_5,
  output out_6
);

  wire and_1_out, and_2_out, and_3_out, dipswitch_1_p1, dipswitch_1_p2, dipswitch_1_p3, dipswitch_1_p4,
       dipswitch_1_p5, dipswitch_1_p6, nor_1_out, nor_2_out, not_1_out, not_2_out, not_3_out, not_4_out,
       or_1_out, xor_1_out, xor_2_out;

  // DipSwitch dipswitch_1: pin names not known; wires that end beside it: dipswitch_1_p1, dipswitch_1_p2, dipswitch_1_p3, dipswitch_1_p4, dipswitch_1_p5, dipswitch_1_p6
  nor nor_1 (nor_1_out, dipswitch_1_p1, dipswitch_1_p2);
  and and_1 (and_1_out, dipswitch_1_p1, dipswitch_1_p2);
  nor nor_2 (nor_2_out, nor_1_out, and_1_out);
  xor xor_1 (xor_1_out, dipswitch_1_p3, dipswitch_1_p4);
  LED led_1 (.in(xor_1_out));
  not not_1 (not_1_out, dipswitch_1_p5);
  not not_2 (not_2_out, dipswitch_1_p6);
  LED led_2 (.in(nor_2_out));
  and and_2 (and_2_out, not_1_out, dipswitch_1_p6);
  and and_3 (and_3_out, dipswitch_1_p5, not_2_out);
  or or_1 (or_1_out, and_2_out, and_3_out);
  LED led_3 (.in(or_1_out));
  not not_3 (not_3_out, in_1);
  and and_4 (out_3, not_3_out, not_4_out);
  not not_4 (not_4_out, in_2);
  and and_5 (out_4, in_1, xor_2_out);
  xor xor_2 (xor_2_out, in_1, in_2);
  and and_6 (out_5, xor_2_out, in_2);
  and and_7 (out_6, in_1, in_2);
endmodule
