// Logisim project F3.3.4 XNOR.circ as structural Verilog: 1 circuit, main circuit main
module main (
  input  in_1,
  input  in_2,
  output out_3
);

  wire transistor_1_out, transistor_2_out, transistor_3_out;

  Transistor transistor_1 (.in(1'b1), .out(transistor_1_out), .gate(in_1));
  Transistor #(.\type ("n")) transistor_2 (.in(transistor_1_out), .out(transistor_2_out), .gate(in_1));
  Transistor transistor_3 (.in(in_2), .out(transistor_3_out), .gate(transistor_1_out));
  Transistor #(.\type ("n")) transistor_4 (.in(transistor_3_out), .out(out_3), .gate(in_1));
  Transistor transistor_5 (.in(transistor_1_out), .out(out_3), .gate(in_2));
  Transistor #(.\type ("n")) transistor_6 (.in(out_3), .out(in_1), .gate(in_2));
  // also tied to GND on the sheet: transistor_2_out

  // Other names for the same wires on the sheet: A = in_1; B = in_2
endmodule
