// Logisim project F3.5.10__MUX2_4.circ as structural Verilog: 1 circuit, main circuit main
module main (
  input  [2:0] in_1,
  input  [2:0] in_2,
  input  [2:0] in_3,
  input  S0,
  input  S1,
  input  [2:0] in_6,
  output [2:0] out_7
);

  wire D0, D1, D2, D3, not_1_out, not_2_out, O00, O01, O02, O10, O11, O12, O20, O21, O22, O30, O31, O32;

  and and_1 (O00, in_1[0], D0);
  and and_2 (O01, in_1[1], D0);
  and and_3 (O02, in_1[2], D0);
  and and_4 (O10, in_2[0], D1);
  and and_5 (O11, in_2[1], D1);
  and and_6 (O12, in_2[2], D1);
  and and_7 (O20, in_3[0], D2);
  and and_8 (O21, in_3[1], D2);
  and and_9 (O22, in_3[2], D2);
  and and_10 (O30, in_6[0], D3);
  and and_11 (O31, in_6[1], D3);
  and and_12 (O32, in_6[2], D3);
  and and_13 (D0, not_1_out, not_2_out);
  not not_1 (not_1_out, S0);
  and and_14 (D1, S0, not_2_out);
  not not_2 (not_2_out, S1);
  or or_1 (out_7[0], O00, O30, O20, O10);
  or or_2 (out_7[1], O01, O11, O21, O31);
  or or_3 (out_7[2], O02, O12, O22, O32);
  and and_15 (D2, not_1_out, S1);
  and and_16 (D3, S0, S1);
endmodule
