// Logisim project F3.5.11__Comparator_4bit.circ as structural Verilog: 1 circuit, main circuit main
module main (
);

  wire A0, A1, A2, A3, and_1_out, B0, B1, B2, B3, xnor_1_out, xnor_2_out, xnor_3_out, xnor_4_out;

  // DipSwitch #(.number(4)) dipswitch_1: pin names not known; wires that end beside it: A0, A1, A2, A3
  // DipSwitch #(.number(4)) dipswitch_2: pin names not known; wires that end beside it: B0, B1, B2, B3
  xnor xnor_1 (xnor_1_out, A0, B0);
  xnor xnor_2 (xnor_2_out, A1, B1);
  xnor xnor_3 (xnor_3_out, A2, B2);
  xnor xnor_4 (xnor_4_out, A3, B3);
  and and_1 (and_1_out, xnor_1_out, xnor_2_out, xnor_3_out, xnor_4_out);
  LED led_1 (.in(and_1_out));
endmodule
