// Logisim project F3.5.15_FAHA.circ as structural Verilog: 2 circuits, main circuit main
module main (
  input  Cin,
  input  A,
  input  B,
  output S,
  output Cout
);

  wire and_1_out, ha_1_c, ha_1_s, or_1_out;

  or or_1 (or_1_out, A, B);
  and and_1 (and_1_out, Cin, or_1_out);
  HA ha_1 (.A(A), .B(B), .S(ha_1_s), .C(ha_1_c));
  xor xor_1 (S, Cin, ha_1_s);
  or or_2 (Cout, ha_1_c, and_1_out);
endmodule

module HA (
  input  A,
  input  B,
  output S,
  output C
);

  xor xor_1 (S, A, B);
  and and_1 (C, A, B);
endmodule
