// Logisim project F3.5.16 Adder.circ as structural Verilog: 3 circuits, main circuit main
module main (
  input  A0,
  input  B0,
  input  A1,
  input  B1,
  input  A2,
  input  B2,
  input  A3,
  input  B3
);

  wire fa_1_cout, fa_2_cout, fa_3_cout, fa_4_cout, S0, S1, S2, S3;

  Hex_Digit_Display #(.decimalPoint("false")) hex_digit_display_1 (.value({A3, A2, A1, A0}));
  Hex_Digit_Display #(.decimalPoint("false")) hex_digit_display_2 (.value({B3, B2, B1, B0}));
  Hex_Digit_Display #(.decimalPoint("false")) hex_digit_display_3 (.value({S3, S2, S1, S0}));
  FA fa_1 (.A(A0), .B(B0), .Cin(1'b0), .S(S0), .Cout(fa_1_cout));
  FA fa_2 (.A(A1), .B(B1), .Cin(fa_1_cout), .S(S1), .Cout(fa_2_cout));
  FA fa_3 (.A(A2), .B(B2), .Cin(fa_2_cout), .S(S2), .Cout(fa_3_cout));
  FA fa_4 (.A(A3), .B(B3), .Cin(fa_3_cout), .S(S3), .Cout(fa_4_cout));
  LED led_1 (.in(fa_4_cout));
endmodule

module FA (
  input  A,
  input  B,
  input  Cin,
  output S,
  output Cout
);

  wire and_1_out, and_2_out, and_3_out, and_4_out, and_5_out, xnor_1_out, xor_1_out;

  xor xor_1 (xor_1_out, A, B);
  and and_1 (and_1_out, A, B);
  and and_2 (and_2_out, B, Cin);
  and and_3 (and_3_out, A, Cin);
  and and_4 (and_4_out, ~Cin, xor_1_out);  // AND_Gate
  xnor xnor_1 (xnor_1_out, A, B);
  and and_5 (and_5_out, xnor_1_out, Cin);
  or or_1 (Cout, and_1_out, and_2_out, and_3_out);
  or or_2 (S, and_4_out, and_5_out);
endmodule

module Dec_7sd (
  input  A0,
  input  A1,
  input  A2,
  input  A3,
  output a,
  output b,
  output c,
  output d,
  output e,
  output f,
  output g
);

  wire L00, L01, L10, L11, NA0, NA1, NA2, NA3, P0, P1, P2, P3, P4, P5, P6, P7, P8, P9, Pa, Pb, Pc, Pd, Pe,
       Pf, R00, R01, R10, R11, xor_1_out, xor_2_out;

  not not_1 (NA0, A0);
  not not_2 (NA1, A1);
  not not_3 (NA2, A2);
  not not_4 (NA3, A3);
  and and_1 (P0, L00, R00);
  and and_2 (P1, L00, R01);
  and and_3 (P2, L00, R10);
  and and_4 (P3, L00, R11);
  and and_5 (P4, L01, R00);
  and and_6 (P5, L01, R01);
  and and_7 (P6, L01, R10);
  and and_8 (P7, L01, R11);
  and and_9 (P8, L10, R00);
  and and_10 (P9, L10, R01);
  and and_11 (Pa, L10, R10);
  and and_12 (Pb, L10, R11);
  and and_13 (Pc, L11, R00);
  and and_14 (Pd, L11, R01);
  and and_15 (Pe, L11, R10);
  and and_16 (Pf, L11, R11);
  and and_17 (R00, NA0, NA1);
  xor xor_1 (xor_1_out, A0, A1);
  and and_18 (R11, A0, A1);
  and and_19 (R01, A0, xor_1_out);
  and and_20 (R10, xor_1_out, A1);
  or or_1 (a, P0, P2, P3, P5, P6, P7, P8, P9, Pa, Pc, Pe, Pf);
  or or_2 (b, P0, P1, P2, P3, P4, P7, P8, P9, Pa, Pd);
  or or_3 (c, P0, P1, P3, P4, P5, P6, P7, P8, P9, Pa, Pb, Pd);
  or or_4 (d, P0, P2, P3, P5, P6, P8, Pb, Pc, Pd, Pe);
  or or_5 (e, P0, P2, P6, P8, Pa, Pb, Pc, Pd, Pe, Pf);
  or or_6 (f, P0, P4, P5, P6, P8, P9, Pa, Pb, Pc, Pe, Pf);
  or or_7 (g, P2, P3, P4, P5, P6, P8, P9, Pa, Pb, Pd, Pe, Pf);
  and and_21 (L00, NA2, NA3);
  xor xor_2 (xor_2_out, A2, A3);
  and and_22 (L11, A2, A3);
  and and_23 (L01, A2, xor_2_out);
  and and_24 (L10, xor_2_out, A3);
endmodule
