// Logisim project F3.5.16__Adder.circ as structural Verilog: 2 circuits, main circuit main
module main (
  input  A0,
  input  B0,
  input  A1,
  input  B1,
  input  A2,
  input  B2,
  input  A3,
  input  B3
);

  wire fa_1_cout, fa_2_cout, fa_3_cout, fa_4_cout, S0, S1, S2, S3;

  Hex_Digit_Display #(.decimalPoint("false")) hex_digit_display_1 (.value({A3, A2, A1, A0}));
  Hex_Digit_Display #(.decimalPoint("false")) hex_digit_display_2 (.value({B3, B2, B1, B0}));
  Hex_Digit_Display #(.decimalPoint("false")) hex_digit_display_3 (.value({S3, S2, S1, S0}));
  FA fa_1 (.A(A0), .B(B0), .Cin(1'b0), .S(S0), .Cout(fa_1_cout));
  FA fa_2 (.A(A1), .B(B1), .Cin(fa_1_cout), .S(S1), .Cout(fa_2_cout));
  FA fa_3 (.A(A2), .B(B2), .Cin(fa_2_cout), .S(S2), .Cout(fa_3_cout));
  FA fa_4 (.A(A3), .B(B3), .Cin(fa_3_cout), .S(S3), .Cout(fa_4_cout));
  LED led_1 (.in(fa_4_cout));
endmodule

module FA (
  input  A,
  input  B,
  input  Cin,
  output S,
  output Cout
);

  wire and_1_out, and_2_out, and_3_out, and_4_out, and_5_out, xnor_1_out, xor_1_out;

  xor xor_1 (xor_1_out, A, B);
  and and_1 (and_1_out, A, B);
  and and_2 (and_2_out, B, Cin);
  and and_3 (and_3_out, A, Cin);
  and and_4 (and_4_out, ~Cin, xor_1_out);  // AND_Gate
  xnor xnor_1 (xnor_1_out, A, B);
  and and_5 (and_5_out, xnor_1_out, Cin);
  or or_1 (Cout, and_1_out, and_2_out, and_3_out);
  or or_2 (S, and_4_out, and_5_out);
endmodule
