// Logisim project F3.5.1_decoder2_4.circ as structural Verilog: 1 circuit, main circuit main
module main (
  input  in_1,
  input  in_2,
  output out_3,
  output out_4,
  output out_5,
  output out_6
);

  wire not_1_out, not_2_out, xor_1_out;

  not not_1 (not_1_out, in_1);
  not not_2 (not_2_out, in_2);
  xor xor_1 (xor_1_out, in_1, in_2);
  and and_1 (out_3, not_1_out, not_2_out);
  and and_2 (out_4, in_1, xor_1_out);
  and and_3 (out_5, xor_1_out, in_2);
  and and_4 (out_6, in_1, in_2);
endmodule
