// Logisim project F3.5.3__decoder3_8.circ as structural Verilog: 2 circuits, main circuit main
module main (
  input  in_1,
  input  in_2,
  input  in_3,
  output out_4,
  output out_5,
  output out_6,
  output out_7,
  output out_8,
  output out_9,
  output out_10,
  output out_11
);

  wire decoder2_4_1_out_3, decoder2_4_1_out_4, decoder2_4_1_out_5, decoder2_4_1_out_6;

  Decoder2_4 decoder2_4_1 (
    .in_1(in_1), .in_2(in_2), .out_3(decoder2_4_1_out_3), .out_4(decoder2_4_1_out_4),
    .out_5(decoder2_4_1_out_5), .out_6(decoder2_4_1_out_6));
  Decoder2_4 decoder2_4_2 (.in_1(decoder2_4_1_out_3), .in_2(in_3), .out_4(out_4), .out_6(out_8));  // open: out_3, out_5
  Decoder2_4 decoder2_4_3 (.in_1(decoder2_4_1_out_4), .in_2(in_3), .out_4(out_5), .out_6(out_9));  // open: out_3, out_5
  Decoder2_4 decoder2_4_4 (
    .in_1(decoder2_4_1_out_5), .in_2(in_3), .out_4(out_6), .out_6(out_10));  // open: out_3, out_5
  Decoder2_4 decoder2_4_5 (
    .in_1(decoder2_4_1_out_6), .in_2(in_3), .out_4(out_7), .out_6(out_11));  // open: out_3, out_5

  // Other names for the same wires on the sheet: A3 = in_3
endmodule

module Decoder2_4 (
  input  in_1,
  input  in_2,
  output out_3,
  output out_4,
  output out_5,
  output out_6
);

  wire not_1_out, not_2_out, xor_1_out;

  not not_1 (not_1_out, in_1);
  not not_2 (not_2_out, in_2);
  xor xor_1 (xor_1_out, in_1, in_2);
  and and_1 (out_3, not_1_out, not_2_out);
  and and_2 (out_4, in_1, xor_1_out);
  and and_3 (out_5, xor_1_out, in_2);
  and and_4 (out_6, in_1, in_2);
endmodule
