// Logisim project F3.5.5_7sDisplayDecoder_2.circ as structural Verilog: 1 circuit, main circuit main
module main (
  input  A0,
  input  A1,
  input  A2,
  input  A3,
  input  in_5
);

  wire a, b, c, d, e, f, g, h, L00, L01, L10, L11, NA0, NA1, NA2, NA3, P0, P1, P2, P3, P4, P5, P6, P7, P8,
       P9, Pa, Pb, Pc, Pd, Pe, Pf, R00, R01, R10, R11, xor_1_out, xor_2_out;

  not not_1 (NA0, A0);
  not not_2 (NA1, A1);
  not not_3 (NA2, A2);
  not not_4 (NA3, A3);
  and and_1 (P0, L00, R00);
  and and_2 (P1, L00, R01);
  and and_3 (P2, L00, R10);
  and and_4 (P3, L00, R11);
  and and_5 (P4, L01, R00);
  and and_6 (P5, L01, R01);
  and and_7 (P6, L01, R10);
  and and_8 (P7, L01, R11);
  and and_9 (P8, L10, R00);
  and and_10 (P9, L10, R01);
  and and_11 (Pa, L10, R10);
  and and_12 (Pb, L10, R11);
  and and_13 (Pc, L11, R00);
  and and_14 (Pd, L11, R01);
  and and_15 (Pe, L11, R10);
  and and_16 (Pf, L11, R11);
  and and_17 (R00, NA0, NA1);
  xor xor_1 (xor_1_out, A0, A1);
  and and_18 (R11, A0, A1);
  and and_19 (R01, A0, xor_1_out);
  and and_20 (R10, xor_1_out, A1);
  or or_1 (a, P0, P2, P3, P5, P6, P7, P8, P9, Pa, Pc, Pe, Pf);
  or or_2 (b, P0, P1, P2, P3, P4, P7, P8, P9, Pa, Pd);
  or or_3 (c, P0, P1, P3, P4, P5, P6, P7, P8, P9, Pa, Pb, Pd);
  or or_4 (d, P0, P2, P3, P5, P6, P8, Pb, Pc, Pd, Pe);
  and and_21 (L00, NA2, NA3);
  xor xor_2 (xor_2_out, A2, A3);
  and and_22 (L11, A2, A3);
  and and_23 (L01, A2, xor_2_out);
  and and_24 (L10, xor_2_out, A3);
  buf or_5 (h, in_5);  // OR_Gate
  or or_6 (e, P0, P2, P6, P8, Pa, Pb, Pc, Pd, Pe, Pf);
  or or_7 (f, P0, P4, P5, P6, P8, P9, Pa, Pb, Pc, Pe, Pf);
  or or_8 (g, P2, P3, P4, P5, P6, P8, P9, Pa, Pb, Pd, Pe, Pf);
  _7_Segment_Display u_7_segment_display_1 (.g(g), .f(f), .a(a), .b(b), .e(e), .d(d), .c(c), .dp(h));
endmodule
