// Logisim project F3.5.7_PENC4_2.circ as structural Verilog: 1 circuit, main circuit main
module main (
  input  A0,
  input  A1,
  input  A2,
  input  A3,
  output Y0,
  output Y1
);

  wire and_1_out, not_1_out;

  not not_1 (not_1_out, A2);
  and and_1 (and_1_out, not_1_out, A1);
  or or_1 (Y0, and_1_out, A3);
  or or_2 (Y1, A2, A3);
endmodule
