// Logisim project F3.5.8_PENC16_4.circ as structural Verilog: 3 circuits, main circuit main
module main (
  input  POINT
);

  wire a, A0, A1, A2, A3, b, c, d, dipswitch_1_p1, dipswitch_1_p2, dipswitch_1_p3, dipswitch_1_p4,
       dipswitch_1_p5, dipswitch_1_p6, dipswitch_1_p7, dipswitch_1_p8, dipswitch_1_p9, dipswitch_1_p10,
       dipswitch_1_p11, dipswitch_1_p12, dipswitch_1_p13, dipswitch_1_p14, dipswitch_1_p15, dipswitch_1_p16,
       e, f, g, h, L00, L01, L10, L11, NA0, NA1, NA2, NA3, P0, P1, P2, P3, P4, P5, P6, P7, P8, P9, Pa, Pb,
       Pc, Pd, Pe, Pf, R00, R01, R10, R11, xor_1_out, xor_2_out;

  not not_1 (NA0, A0);
  not not_2 (NA1, A1);
  not not_3 (NA2, A2);
  not not_4 (NA3, A3);
  and and_1 (P0, L00, R00);
  and and_2 (P1, L00, R01);
  and and_3 (P2, L00, R10);
  and and_4 (P3, L00, R11);
  and and_5 (P4, L01, R00);
  and and_6 (P5, L01, R01);
  and and_7 (P6, L01, R10);
  and and_8 (P7, L01, R11);
  and and_9 (P8, L10, R00);
  and and_10 (P9, L10, R01);
  and and_11 (Pa, L10, R10);
  and and_12 (Pb, L10, R11);
  and and_13 (Pc, L11, R00);
  and and_14 (Pd, L11, R01);
  and and_15 (Pe, L11, R10);
  and and_16 (Pf, L11, R11);
  and and_17 (R00, NA0, NA1);
  xor xor_1 (xor_1_out, A0, A1);
  and and_18 (R11, A0, A1);
  and and_19 (R01, A0, xor_1_out);
  and and_20 (R10, xor_1_out, A1);
  or or_1 (a, P0, P2, P3, P5, P6, P7, P8, P9, Pa, Pc, Pe, Pf);
  or or_2 (b, P0, P1, P2, P3, P4, P7, P8, P9, Pa, Pd);
  or or_3 (c, P0, P1, P3, P4, P5, P6, P7, P8, P9, Pa, Pb, Pd);
  or or_4 (d, P0, P2, P3, P5, P6, P8, Pb, Pc, Pd, Pe);
  and and_21 (L00, NA2, NA3);
  xor xor_2 (xor_2_out, A2, A3);
  and and_22 (L11, A2, A3);
  and and_23 (L01, A2, xor_2_out);
  and and_24 (L10, xor_2_out, A3);
  buf or_5 (h, POINT);  // OR_Gate
  or or_6 (e, P0, P2, P6, P8, Pa, Pb, Pc, Pd, Pe, Pf);
  or or_7 (f, P0, P4, P5, P6, P8, P9, Pa, Pb, Pc, Pe, Pf);
  or or_8 (g, P2, P3, P4, P5, P6, P8, P9, Pa, Pb, Pd, Pe, Pf);
  // DipSwitch #(.number(16)) dipswitch_1: pin names not known; wires that end beside it: dipswitch_1_p1, dipswitch_1_p2, dipswitch_1_p3, dipswitch_1_p4, dipswitch_1_p5, dipswitch_1_p6, dipswitch_1_p7, dipswitch_1_p8, dipswitch_1_p9, dipswitch_1_p10, dipswitch_1_p11, dipswitch_1_p12, dipswitch_1_p13, dipswitch_1_p14, dipswitch_1_p15, dipswitch_1_p16
  _7_Segment_Display u_7_segment_display_1 (.g(g), .f(f), .a(a), .b(b), .e(e), .d(d), .c(c), .dp(h));
  PENC16_4 penc16_4_1 (
    .in_1(dipswitch_1_p1), .in_2(dipswitch_1_p2), .in_3(dipswitch_1_p3), .in_4(dipswitch_1_p4),
    .in_5(dipswitch_1_p5), .in_6(dipswitch_1_p6), .in_7(dipswitch_1_p7), .in_8(dipswitch_1_p8),
    .in_9(dipswitch_1_p9), .in_10(dipswitch_1_p10), .in_11(dipswitch_1_p11), .in_12(dipswitch_1_p12),
    .in_13(dipswitch_1_p13), .in_14(dipswitch_1_p14), .in_15(dipswitch_1_p15), .in_16(dipswitch_1_p16),
    .Y0(A0), .Y1(A1), .Y2(A2), .Y3(A3));

  // Other names for the same wires on the sheet: Y0 = A0; Y1 = A1; Y2 = A2; Y3 = A3
endmodule

module PENC4_2 (
  input  A0,
  input  A1,
  input  A2,
  input  A3,
  output Y0,
  output Y1
);

  wire and_1_out, not_1_out;

  not not_1 (not_1_out, A2);
  and and_1 (and_1_out, not_1_out, A1);
  or or_1 (Y0, and_1_out, A3);
  or or_2 (Y1, A2, A3);
endmodule

module PENC16_4 (
  input  in_1,
  input  in_2,
  input  in_3,
  input  in_4,
  input  in_5,
  input  in_6,
  input  in_7,
  input  in_8,
  input  in_9,
  input  in_10,
  input  in_11,
  input  in_12,
  input  in_13,
  input  in_14,
  input  in_15,
  input  in_16,
  output Y0,
  output Y1,
  output Y2,
  output Y3
);

  wire EA04, EA05, EA06, EA07, EN0, EN1, EN2, EN3, EY0_0, EY0_1, EY1_0, EY1_1, EY2_0, EY2_1, Y0_0, Y0_1,
       Y1_0, Y1_1, Y2_0, Y2_1, Y3_0, Y3_1;

  or or_1 (EN0, in_1, in_2, in_3, in_4);
  or or_2 (EN1, in_5, in_6, in_7, in_8);
  or or_3 (EN2, in_9, in_10, in_11, in_12);
  or or_4 (EN3, in_13, in_14, in_15, in_16);
  PENC4_2 penc4_2_1 (.A0(in_1), .A1(in_2), .A2(in_3), .A3(in_4), .Y0(Y0_0), .Y1(Y0_1));
  PENC4_2 penc4_2_2 (.A0(in_5), .A1(in_6), .A2(in_7), .A3(in_8), .Y0(Y1_0), .Y1(Y1_1));
  PENC4_2 penc4_2_3 (.A0(in_9), .A1(in_10), .A2(in_11), .A3(in_12), .Y0(Y2_0), .Y1(Y2_1));
  PENC4_2 penc4_2_4 (.A0(in_13), .A1(in_14), .A2(in_15), .A3(in_16), .Y0(Y3_0), .Y1(Y3_1));
  and and_1 (EY0_0, Y0_0, ~EN1, ~EN2, ~EN3);  // AND_Gate
  and and_2 (EY0_1, Y0_1, ~EN1, ~EN2, ~EN3);  // AND_Gate
  and and_3 (EY1_0, Y1_0, ~EN2, ~EN3);  // AND_Gate
  and and_4 (EY1_1, Y1_1, ~EN2, ~EN3);  // AND_Gate
  and and_5 (EY2_0, Y2_0, ~EN3);  // AND_Gate
  and and_6 (EY2_1, Y2_1, ~EN3);  // AND_Gate
  and and_7 (EA04, in_5, ~EN2);  // AND_Gate
  and and_8 (EA05, in_6, ~EN2);  // AND_Gate
  and and_9 (EA06, in_7, ~EN2);  // AND_Gate
  and and_10 (EA07, in_8, ~EN2);  // AND_Gate
  or or_5 (Y0, EY0_0, EY1_0, EY2_0, Y3_0);
  or or_6 (Y1, EY0_1, EY1_1, EY2_1, Y3_1);
  or or_7 (Y2, EA04, EA05, EA06, EA07, in_13, in_14, in_15, in_16);
  or or_8 (Y3, in_9, in_10, in_11, in_12, in_13, in_14, in_15, in_16);

  // Other names for the same wires on the sheet: A00 = in_1; A01 = in_2; A02 = in_3; A03 = in_4; A04 = in_5;
  //   A05 = in_6; A06 = in_7; A07 = in_8; A08 = in_9; A09 = in_10; A10 = in_11; A11 = in_12; A12 = in_13; A13 = in_14;
  //   A14 = in_15; A15 = in_16
endmodule
