// Logisim project F3.6.1_4bitsSubtractor.circ as structural Verilog: 2 circuits, main circuit main
module main (
  input  A0,
  input  B0,
  input  A1,
  input  B1,
  input  A2,
  input  B2,
  input  A3,
  input  B3
);

  wire fs_1_cout, fs_2_cout, fs_3_cout, fs_4_cout, S0, S1, S2, S3;

  Hex_Digit_Display #(.decimalPoint("false")) hex_digit_display_1 (.value({A3, A2, A1, A0}));
  Hex_Digit_Display #(.decimalPoint("false")) hex_digit_display_2 (.value({B3, B2, B1, B0}));
  Hex_Digit_Display #(.decimalPoint("false")) hex_digit_display_3 (.value({S3, S2, S1, S0}));
  FS fs_1 (.A(A0), .B(B0), .Cin(1'b0), .D(S0), .Cout(fs_1_cout));
  FS fs_2 (.A(A1), .B(B1), .Cin(fs_1_cout), .D(S1), .Cout(fs_2_cout));
  FS fs_3 (.A(A2), .B(B2), .Cin(fs_2_cout), .D(S2), .Cout(fs_3_cout));
  FS fs_4 (.A(A3), .B(B3), .Cin(fs_3_cout), .D(S3), .Cout(fs_4_cout));
  LED led_1 (.in(fs_4_cout));
endmodule

module FS (
  input  A,
  input  B,
  input  Cin,
  output D,
  output Cout
);

  wire and_1_out, and_2_out, and_3_out, not_1_out;

  not not_1 (not_1_out, A);
  and and_1 (and_1_out, not_1_out, B);
  and and_2 (and_2_out, not_1_out, Cin);
  and and_3 (and_3_out, B, Cin);
  ExactlyOne xor_1 (.out(D), .in0(A), .in1(B), .in2(Cin));
  or or_1 (Cout, and_1_out, and_2_out, and_3_out);
endmodule
