// Logisim project F3.6.2__samAdder.circ as structural Verilog: 1 circuit, main circuit main
module main (
  input  in_1,
  input  in_2,
  input  in_3,
  input  in_4,
  input  in_5,
  input  in_6,
  input  in_7,
  input  in_8
);

  wire and_1_out, and_2_out, and_3_out, comparator_1_eq, comparator_1_gt, not_1_out, ns, or_2_out, s,
       xor_1_out;
  wire [3:0] adder_1_out, multiplexer_1_out, multiplexer_2_out, multiplexer_3_out, subtractor_1_out;

  _7_Segment_Display u_7_segment_display_1 (.g(in_1));  // open: f, a, b, e, d, c, dp
  Hex_Digit_Display hex_digit_display_1 (.value({1'b0, in_4, in_3, in_2}));  // open: dp
  Comparator #(.mode("unsigned"), .width(4)) comparator_1 (
    .a({1'b0, in_4, in_3, in_2}), .b({1'b0, in_8, in_7, in_6}), .gt(comparator_1_gt), .eq(comparator_1_eq),
    .lt(s));
  _7_Segment_Display u_7_segment_display_2 (.g(in_5));  // open: f, a, b, e, d, c, dp
  Hex_Digit_Display hex_digit_display_2 (.value({1'b0, in_8, in_7, in_6}));  // open: dp
  or or_1 (ns, comparator_1_gt, comparator_1_eq);
  and and_1 (and_1_out, ns, in_1);
  and and_2 (and_2_out, s, in_5);
  and and_3 (and_3_out, in_1, in_5);
  Multiplexer #(.width(4)) multiplexer_1 (
    .in0({1'b0, in_4, in_3, in_2}), .in1({1'b0, in_8, in_7, in_6}), .out(multiplexer_1_out), .sel(s));
  Multiplexer #(.width(4)) multiplexer_2 (
    .in0({1'b0, in_4, in_3, in_2}), .in1({1'b0, in_8, in_7, in_6}), .out(multiplexer_2_out), .sel(not_1_out));
  not not_1 (not_1_out, s);
  or or_2 (or_2_out, and_1_out, and_2_out, and_3_out);
  _7_Segment_Display u_7_segment_display_3 (.g(or_2_out));  // open: f, a, b, e, d, c, dp
  Adder #(.width(4)) adder_1 (
    .a({1'b0, in_4, in_3, in_2}), .b({1'b0, in_8, in_7, in_6}), .out(adder_1_out));  // open: cin, cout
  xor xor_1 (xor_1_out, in_1, in_5);
  Subtractor #(.width(4)) subtractor_1 (
    .a(multiplexer_1_out), .b(multiplexer_2_out), .out(subtractor_1_out));  // open: bin, bout
  Hex_Digit_Display hex_digit_display_3 (.value(multiplexer_3_out));  // open: dp
  Multiplexer #(.width(4)) multiplexer_3 (
    .in0(adder_1_out), .in1(subtractor_1_out), .out(multiplexer_3_out), .sel(xor_1_out));

  // Other names for the same wires on the sheet: A[2:0] = {in_4, in_3, in_2}; B[2:0] = {in_8, in_7, in_6}; S1 = in_1;
  //   S2 = in_5
endmodule
