// Logisim project F3.6.3__OnesComplementAdder.circ as structural Verilog: 2 circuits, main circuit main
module main (
  input  A0,
  input  A1,
  input  A2,
  input  A3,
  input  B0,
  input  B1,
  input  B2,
  input  B3,
  output S0,
  output S1,
  output S2,
  output S3
);

  wire multiplexer_1_out, multiplexer_2_out, multiplexer_3_out, multiplexer_4_out, multiplexer_5_out,
       multiplexer_6_out, not_1_out, not_2_out, not_3_out, not_4_out, not_5_out, not_6_out, not_7_out,
       not_8_out, not_9_out;
  wire [3:0] samadder_1_data;

  not not_1 (not_1_out, A0);
  not not_2 (not_2_out, A1);
  not not_3 (not_3_out, A2);
  not not_4 (not_4_out, B0);
  not not_5 (not_5_out, B1);
  not not_6 (not_6_out, B2);
  Multiplexer multiplexer_1 (.in0(A0), .in1(not_1_out), .out(multiplexer_1_out), .sel(A3));
  Multiplexer multiplexer_2 (.in0(A1), .in1(not_2_out), .out(multiplexer_2_out), .sel(A3));
  Multiplexer multiplexer_3 (.in0(A2), .in1(not_3_out), .out(multiplexer_3_out), .sel(A3));
  Multiplexer multiplexer_4 (.in0(B0), .in1(not_4_out), .out(multiplexer_4_out), .sel(B3));
  Multiplexer multiplexer_5 (.in0(B1), .in1(not_5_out), .out(multiplexer_5_out), .sel(B3));
  Multiplexer multiplexer_6 (.in0(B2), .in1(not_6_out), .out(multiplexer_6_out), .sel(B3));
  SAMadder samadder_1 (
    .A0(multiplexer_1_out), .A1(multiplexer_2_out), .A2(multiplexer_3_out), .A3(A3), .B0(multiplexer_4_out),
    .B1(multiplexer_5_out), .B2(multiplexer_6_out), .B3(B3), .Sign(S3), .data(samadder_1_data));
  not not_7 (not_7_out, samadder_1_data[0]);
  not not_8 (not_8_out, samadder_1_data[1]);
  not not_9 (not_9_out, samadder_1_data[2]);
  Multiplexer multiplexer_7 (.in0(samadder_1_data[0]), .in1(not_7_out), .out(S0), .sel(S3));
  Multiplexer multiplexer_8 (.in0(samadder_1_data[1]), .in1(not_8_out), .out(S1), .sel(S3));
  Multiplexer multiplexer_9 (.in0(samadder_1_data[2]), .in1(not_9_out), .out(S2), .sel(S3));
  _7_Segment_Display u_7_segment_display_1 (.g(S3));  // open: f, a, b, e, d, c, dp
  Hex_Digit_Display hex_digit_display_1 (.value(samadder_1_data));  // open: dp
endmodule

module SAMadder (
  input  A0,
  input  A1,
  input  A2,
  input  A3,
  input  B0,
  input  B1,
  input  B2,
  input  B3,
  output Sign,
  output [3:0] data
);

  wire and_1_out, and_2_out, and_3_out, comparator_1_eq, comparator_1_gt, not_1_out, ns, s, xor_1_out;
  wire [3:0] adder_1_out, multiplexer_1_out, multiplexer_2_out, subtractor_1_out;

  Comparator #(.mode("unsigned"), .width(4)) comparator_1 (
    .a({1'b0, A2, A1, A0}), .b({1'b0, B2, B1, B0}), .gt(comparator_1_gt), .eq(comparator_1_eq), .lt(s));
  or or_1 (ns, comparator_1_gt, comparator_1_eq);
  not not_1 (not_1_out, s);
  and and_1 (and_1_out, ns, A3);
  and and_2 (and_2_out, s, B3);
  and and_3 (and_3_out, A3, B3);
  Adder #(.width(4)) adder_1 (.a({1'b0, A2, A1, A0}), .b({1'b0, B2, B1, B0}), .out(adder_1_out));  // open: cin, cout
  Multiplexer #(.width(4)) multiplexer_1 (
    .in0({1'b0, A2, A1, A0}), .in1({1'b0, B2, B1, B0}), .out(multiplexer_1_out), .sel(s));
  Subtractor #(.width(4)) subtractor_1 (
    .a(multiplexer_1_out), .b(multiplexer_2_out), .out(subtractor_1_out));  // open: bin, bout
  Multiplexer #(.width(4)) multiplexer_2 (
    .in0({1'b0, A2, A1, A0}), .in1({1'b0, B2, B1, B0}), .out(multiplexer_2_out), .sel(not_1_out));
  or or_2 (Sign, and_1_out, and_2_out, and_3_out);
  Multiplexer #(.width(4)) multiplexer_3 (.in0(adder_1_out), .in1(subtractor_1_out), .out(data), .sel(xor_1_out));
  xor xor_1 (xor_1_out, A3, B3);

  // Other names for the same wires on the sheet: S1 = A3; S2 = B3
endmodule
