// Logisim project F3.6.3__OnesComplementAdder2.circ as structural Verilog: 2 circuits, main circuit main
module main (
  input  A0,
  input  B0,
  input  A1,
  input  B1,
  input  A2,
  input  B2,
  input  A3,
  input  B3,
  output C0,
  output C1,
  output C2,
  output C3
);

  wire cout, fa_1_cout, fa_2_cout, fa_3_cout, fa_4_cout, fa_5_cout, fa_6_cout, fa_8_cout, S0, S1, S2, S3,
       SS0, SS1, SS2, SS3;

  Multiplexer multiplexer_1 (.in0(S0), .in1(SS0), .out(C0), .sel(cout));
  Multiplexer multiplexer_2 (.in0(S1), .in1(SS1), .out(C1), .sel(cout));
  Multiplexer multiplexer_3 (.in0(S2), .in1(SS2), .out(C2), .sel(cout));
  Multiplexer multiplexer_4 (.in0(S3), .in1(SS3), .out(C3), .sel(cout));
  FA fa_1 (.A(A0), .B(B0), .Cin(1'b0), .S(S0), .Cout(fa_1_cout));
  FA fa_2 (.A(S0), .B(1'b1), .Cin(1'b0), .S(SS0), .Cout(fa_2_cout));
  FA fa_3 (.A(A1), .B(B1), .Cin(fa_1_cout), .S(S1), .Cout(fa_3_cout));
  FA fa_4 (.A(S1), .B(1'b0), .Cin(fa_2_cout), .S(SS1), .Cout(fa_4_cout));
  FA fa_5 (.A(A2), .B(B2), .Cin(fa_3_cout), .S(S2), .Cout(fa_5_cout));
  FA fa_6 (.A(S2), .B(1'b0), .Cin(fa_4_cout), .S(SS2), .Cout(fa_6_cout));
  FA fa_7 (.A(A3), .B(B3), .Cin(fa_5_cout), .S(S3), .Cout(cout));
  FA fa_8 (.A(S3), .B(1'b0), .Cin(fa_6_cout), .S(SS3), .Cout(fa_8_cout));
  LED led_1 (.in(fa_8_cout));
endmodule

module FA (
  input  A,
  input  B,
  input  Cin,
  output S,
  output Cout
);

  wire and_1_out, and_2_out, and_3_out, and_4_out, and_5_out, xnor_1_out, xor_1_out;

  xor xor_1 (xor_1_out, A, B);
  and and_1 (and_1_out, A, B);
  and and_2 (and_2_out, B, Cin);
  and and_3 (and_3_out, A, Cin);
  and and_4 (and_4_out, ~Cin, xor_1_out);  // AND_Gate
  xnor xnor_1 (xnor_1_out, A, B);
  and and_5 (and_5_out, xnor_1_out, Cin);
  or or_1 (Cout, and_1_out, and_2_out, and_3_out);
  or or_2 (S, and_4_out, and_5_out);
endmodule
