// Logisim project F3.7.10_ENDFF.circ as structural Verilog: 2 circuits, main circuit main
module main (
  input  D,
  input  EN,
  output Q
);

  wire clk_out, dlatch_1_q, multiplexer_1_out, not_1_out;

  Multiplexer multiplexer_1 (.in0(Q), .in1(D), .out(multiplexer_1_out), .sel(EN));
  Clock clk (.out(clk_out));
  not not_1 (not_1_out, clk_out);
  Dlatch dlatch_1 (.D(multiplexer_1_out), .WE(not_1_out), .Q(dlatch_1_q));  // open: NQ
  Dlatch dlatch_2 (.D(dlatch_1_q), .WE(clk_out), .Q(Q));  // open: NQ
endmodule

module Dlatch (
  input  D,
  input  WE,
  output Q,
  output NQ
);

  wire and_1_out, and_2_out, not_1_out;

  not not_1 (not_1_out, D);
  and and_1 (and_1_out, D, WE);
  and and_2 (and_2_out, WE, not_1_out);
  nor nor_1 (NQ, and_1_out, Q);
  nor nor_2 (Q, NQ, and_2_out);
endmodule
