// Logisim project F3.7.12_4bitRegister.circ as structural Verilog: 3 circuits, main circuit main
module main (
  input  R,
  input  EN
);

  wire clk_out;
  wire [3:0] dff_1_q, dipswitch_1_p1;

  // DipSwitch #(.number(4)) dipswitch_1: pin names not known; wires that end beside it: dipswitch_1_p1[0], dipswitch_1_p1[1], dipswitch_1_p1[2], dipswitch_1_p1[3]
  Hex_Digit_Display hex_digit_display_1 (.value(dipswitch_1_p1));  // open: dp
  Clock clk (.out(clk_out));
  DFF dff_1 (.D(dipswitch_1_p1[0]), .R(R), .EN(EN), .CLK(clk_out), .Q(dff_1_q[0]));  // open: NQ
  DFF dff_2 (.D(dipswitch_1_p1[1]), .R(R), .EN(EN), .CLK(clk_out), .Q(dff_1_q[1]));  // open: NQ
  DFF dff_3 (.D(dipswitch_1_p1[2]), .R(R), .EN(EN), .CLK(clk_out), .Q(dff_1_q[2]));  // open: NQ
  DFF dff_4 (.D(dipswitch_1_p1[3]), .R(R), .EN(EN), .CLK(clk_out), .Q(dff_1_q[3]));  // open: NQ
  Hex_Digit_Display hex_digit_display_2 (.value(dff_1_q));  // open: dp
endmodule

module Dlatch (
  input  D,
  input  WE,
  output Q,
  output NQ
);

  wire and_1_out, and_2_out, not_1_out;

  not not_1 (not_1_out, D);
  and and_1 (and_1_out, D, WE);
  and and_2 (and_2_out, WE, not_1_out);
  nor nor_1 (NQ, and_1_out, Q);
  nor nor_2 (Q, NQ, and_2_out);
endmodule

module DFF (
  input  D,
  input  R,
  input  EN,
  input  CLK,
  output Q,
  output NQ
);

  wire and_1_out, and_2_out, dlatch_1_q, multiplexer_1_out, not_1_out, not_2_out, or_1_out, or_2_out;

  Multiplexer multiplexer_1 (.in0(Q), .in1(D), .out(multiplexer_1_out), .sel(EN));
  not not_1 (not_1_out, CLK);
  not not_2 (not_2_out, R);
  or or_1 (or_1_out, not_1_out, R);
  and and_1 (and_1_out, not_2_out, multiplexer_1_out);
  Dlatch dlatch_1 (.D(and_1_out), .WE(or_1_out), .Q(dlatch_1_q));  // open: NQ
  or or_2 (or_2_out, CLK, R);
  and and_2 (and_2_out, not_2_out, dlatch_1_q);
  Dlatch dlatch_2 (.D(and_2_out), .WE(or_2_out), .Q(Q), .NQ(NQ));
endmodule
