// Logisim project F3.7.13_4bitcounter.circ as structural Verilog: 5 circuits, main circuit main
module main (
  input  R,
  input  EN
);

  wire clk_out;
  wire [3:0] add_1_s0, dff_1_q;

  Hex_Digit_Display hex_digit_display_1 (.value(add_1_s0));  // open: dp
  Clock clk (.out(clk_out));
  DFF dff_1 (.D(add_1_s0[0]), .R(R), .EN(EN), .CLK(clk_out), .Q(dff_1_q[0]));  // open: NQ
  DFF dff_2 (.D(add_1_s0[1]), .R(R), .EN(EN), .CLK(clk_out), .Q(dff_1_q[1]));  // open: NQ
  DFF dff_3 (.D(add_1_s0[2]), .R(R), .EN(EN), .CLK(clk_out), .Q(dff_1_q[2]));  // open: NQ
  DFF dff_4 (.D(add_1_s0[3]), .R(R), .EN(EN), .CLK(clk_out), .Q(dff_1_q[3]));  // open: NQ
  Hex_Digit_Display hex_digit_display_2 (.value(dff_1_q));  // open: dp
  add add_1 (
    .A0(dff_1_q[0]), .B0(1'b1), .A1(dff_1_q[1]), .B1(1'b0), .A2(dff_1_q[2]), .B2(1'b0), .A3(dff_1_q[3]),
    .B3(1'b0), .S0(add_1_s0[0]), .S1(add_1_s0[1]), .S2(add_1_s0[2]), .S3(add_1_s0[3]));
endmodule

module Dlatch (
  input  D,
  input  WE,
  output Q,
  output NQ
);

  wire and_1_out, and_2_out, not_1_out;

  not not_1 (not_1_out, D);
  and and_1 (and_1_out, D, WE);
  and and_2 (and_2_out, WE, not_1_out);
  nor nor_1 (NQ, and_1_out, Q);
  nor nor_2 (Q, NQ, and_2_out);
endmodule

module DFF (
  input  D,
  input  R,
  input  EN,
  input  CLK,
  output Q,
  output NQ
);

  wire and_1_out, and_2_out, dlatch_1_q, multiplexer_1_out, not_1_out, not_2_out, or_1_out, or_2_out;

  Multiplexer multiplexer_1 (.in0(Q), .in1(D), .out(multiplexer_1_out), .sel(EN));
  not not_1 (not_1_out, CLK);
  not not_2 (not_2_out, R);
  or or_1 (or_1_out, not_1_out, R);
  and and_1 (and_1_out, not_2_out, multiplexer_1_out);
  Dlatch dlatch_1 (.D(and_1_out), .WE(or_1_out), .Q(dlatch_1_q));  // open: NQ
  or or_2 (or_2_out, CLK, R);
  and and_2 (and_2_out, not_2_out, dlatch_1_q);
  Dlatch dlatch_2 (.D(and_2_out), .WE(or_2_out), .Q(Q), .NQ(NQ));
endmodule

module FA (
  input  A,
  input  B,
  input  Cin,
  output S,
  output Cout
);

  wire and_1_out, and_2_out, and_3_out, and_4_out, and_5_out, xnor_1_out, xor_1_out;

  xor xor_1 (xor_1_out, A, B);
  and and_1 (and_1_out, A, B);
  and and_2 (and_2_out, B, Cin);
  and and_3 (and_3_out, A, Cin);
  and and_4 (and_4_out, ~Cin, xor_1_out);  // AND_Gate
  xnor xnor_1 (xnor_1_out, A, B);
  and and_5 (and_5_out, xnor_1_out, Cin);
  or or_1 (Cout, and_1_out, and_2_out, and_3_out);
  or or_2 (S, and_4_out, and_5_out);
endmodule

module add (
  input  A0,
  input  B0,
  input  A1,
  input  B1,
  input  A2,
  input  B2,
  input  A3,
  input  B3,
  output S0,
  output S1,
  output S2,
  output S3
);

  wire fa_1_cout, fa_2_cout, fa_3_cout, fa_4_cout;

  FA fa_1 (.A(A0), .B(B0), .Cin(1'b0), .S(S0), .Cout(fa_1_cout));
  FA fa_2 (.A(A1), .B(B1), .Cin(fa_1_cout), .S(S1), .Cout(fa_2_cout));
  FA fa_3 (.A(A2), .B(B2), .Cin(fa_2_cout), .S(S2), .Cout(fa_3_cout));
  FA fa_4 (.A(A3), .B(B3), .Cin(fa_3_cout), .S(S3), .Cout(fa_4_cout));
  LED led_1 (.in(fa_4_cout));
endmodule
