// Logisim project F3.7.14_series.circ as structural Verilog: 6 circuits, main circuit main
module main (
  input  clear,
  input  R,
  input  EN
);

  wire adder8bit_1_s0, adder8bit_1_s1, adder8bit_1_s2, adder8bit_1_s3, adder8bit_1_s4, adder8bit_1_s5,
       adder8bit_1_s6, adder8bit_1_s7, CLK2_out, clk_out, comparator_1_gt, dff_5_q, dff_6_q, dff_7_q,
       dff_8_q, dff_9_q, dff_10_q, dff_11_q, dff_12_q, not_1_out;
  wire [3:0] adder4bit_1_s0, dff_1_q;

  Hex_Digit_Display hex_digit_display_1 (.value(adder4bit_1_s0));  // open: dp
  Clock clk (.out(clk_out));
  DFF dff_1 (.D(adder4bit_1_s0[0]), .R(R), .EN(EN), .CLK(clk_out), .Q(dff_1_q[0]));  // open: NQ
  DFF dff_2 (.D(adder4bit_1_s0[1]), .R(R), .EN(EN), .CLK(clk_out), .Q(dff_1_q[1]));  // open: NQ
  DFF dff_3 (.D(adder4bit_1_s0[2]), .R(R), .EN(EN), .CLK(clk_out), .Q(dff_1_q[2]));  // open: NQ
  DFF dff_4 (.D(adder4bit_1_s0[3]), .R(R), .EN(EN), .CLK(clk_out), .Q(dff_1_q[3]));  // open: NQ
  Hex_Digit_Display hex_digit_display_2 (.value(dff_1_q));  // open: dp
  Comparator #(.mode("unsigned"), .width(4)) comparator_1 (
    .a(4'b1011), .b(dff_1_q), .gt(comparator_1_gt));  // open: eq, lt
  adder4bit adder4bit_1 (
    .A0(dff_1_q[0]), .B0(1'b1), .A1(dff_1_q[1]), .B1(1'b0), .A2(dff_1_q[2]), .B2(1'b0), .A3(dff_1_q[3]),
    .B3(1'b0), .S0(adder4bit_1_s0[0]), .S1(adder4bit_1_s0[1]), .S2(adder4bit_1_s0[2]), .S3(adder4bit_1_s0[3]));
  adder8bit adder8bit_1 (
    .A0(adder4bit_1_s0[0]), .B0(dff_5_q), .A1(adder4bit_1_s0[1]), .B1(dff_6_q), .A2(adder4bit_1_s0[2]),
    .B2(dff_7_q), .A3(adder4bit_1_s0[3]), .B3(dff_8_q), .A4(1'b0), .B4(dff_9_q), .A5(1'b0), .B5(dff_10_q),
    .A6(1'b0), .B6(dff_11_q), .A7(1'b0), .B7(dff_12_q), .S0(adder8bit_1_s0), .S1(adder8bit_1_s1),
    .S2(adder8bit_1_s2), .S3(adder8bit_1_s3), .S4(adder8bit_1_s4), .S5(adder8bit_1_s5), .S6(adder8bit_1_s6),
    .S7(adder8bit_1_s7));
  Clock CLK2 (.out(CLK2_out));
  not not_1 (not_1_out, CLK2_out);
  DFF dff_5 (.D(adder8bit_1_s0), .R(clear), .EN(comparator_1_gt), .CLK(not_1_out), .Q(dff_5_q));  // open: NQ
  DFF dff_6 (.D(adder8bit_1_s1), .R(clear), .EN(comparator_1_gt), .CLK(not_1_out), .Q(dff_6_q));  // open: NQ
  DFF dff_7 (.D(adder8bit_1_s2), .R(clear), .EN(comparator_1_gt), .CLK(not_1_out), .Q(dff_7_q));  // open: NQ
  DFF dff_8 (.D(adder8bit_1_s3), .R(clear), .EN(comparator_1_gt), .CLK(not_1_out), .Q(dff_8_q));  // open: NQ
  DFF dff_9 (.D(adder8bit_1_s4), .R(clear), .EN(comparator_1_gt), .CLK(not_1_out), .Q(dff_9_q));  // open: NQ
  DFF dff_10 (.D(adder8bit_1_s5), .R(clear), .EN(comparator_1_gt), .CLK(not_1_out), .Q(dff_10_q));  // open: NQ
  DFF dff_11 (.D(adder8bit_1_s6), .R(clear), .EN(comparator_1_gt), .CLK(not_1_out), .Q(dff_11_q));  // open: NQ
  DFF dff_12 (.D(adder8bit_1_s7), .R(clear), .EN(comparator_1_gt), .CLK(not_1_out), .Q(dff_12_q));  // open: NQ
endmodule

module Dlatch (
  input  D,
  input  WE,
  output Q,
  output NQ
);

  wire and_1_out, and_2_out, not_1_out;

  not not_1 (not_1_out, D);
  and and_1 (and_1_out, D, WE);
  and and_2 (and_2_out, WE, not_1_out);
  nor nor_1 (NQ, and_1_out, Q);
  nor nor_2 (Q, NQ, and_2_out);
endmodule

module DFF (
  input  D,
  input  R,
  input  EN,
  input  CLK,
  output Q,
  output NQ
);

  wire and_1_out, and_2_out, dlatch_1_q, multiplexer_1_out, not_1_out, not_2_out, or_1_out, or_2_out;

  Multiplexer multiplexer_1 (.in0(Q), .in1(D), .out(multiplexer_1_out), .sel(EN));
  not not_1 (not_1_out, CLK);
  not not_2 (not_2_out, R);
  or or_1 (or_1_out, not_1_out, R);
  and and_1 (and_1_out, not_2_out, multiplexer_1_out);
  Dlatch dlatch_1 (.D(and_1_out), .WE(or_1_out), .Q(dlatch_1_q));  // open: NQ
  or or_2 (or_2_out, CLK, R);
  and and_2 (and_2_out, not_2_out, dlatch_1_q);
  Dlatch dlatch_2 (.D(and_2_out), .WE(or_2_out), .Q(Q), .NQ(NQ));
endmodule

module FA (
  input  A,
  input  B,
  input  Cin,
  output S,
  output Cout
);

  wire and_1_out, and_2_out, and_3_out, and_4_out, and_5_out, xnor_1_out, xor_1_out;

  xor xor_1 (xor_1_out, A, B);
  and and_1 (and_1_out, A, B);
  and and_2 (and_2_out, B, Cin);
  and and_3 (and_3_out, A, Cin);
  and and_4 (and_4_out, ~Cin, xor_1_out);  // AND_Gate
  xnor xnor_1 (xnor_1_out, A, B);
  and and_5 (and_5_out, xnor_1_out, Cin);
  or or_1 (Cout, and_1_out, and_2_out, and_3_out);
  or or_2 (S, and_4_out, and_5_out);
endmodule

module adder8bit (
  input  A0,
  input  B0,
  input  A1,
  input  B1,
  input  A2,
  input  B2,
  input  A3,
  input  B3,
  input  A4,
  input  B4,
  input  A5,
  input  B5,
  input  A6,
  input  B6,
  input  A7,
  input  B7,
  output S0,
  output S1,
  output S2,
  output S3,
  output S4,
  output S5,
  output S6,
  output S7
);

  wire fa_1_cout, fa_2_cout, fa_3_cout, fa_4_cout, fa_5_cout, fa_6_cout, fa_7_cout, fa_8_cout;

  FA fa_1 (.A(A0), .B(B0), .Cin(1'b0), .S(S0), .Cout(fa_1_cout));
  FA fa_2 (.A(A1), .B(B1), .Cin(fa_1_cout), .S(S1), .Cout(fa_2_cout));
  FA fa_3 (.A(A2), .B(B2), .Cin(fa_2_cout), .S(S2), .Cout(fa_3_cout));
  FA fa_4 (.A(A3), .B(B3), .Cin(fa_3_cout), .S(S3), .Cout(fa_4_cout));
  FA fa_5 (.A(A4), .B(B4), .Cin(fa_4_cout), .S(S4), .Cout(fa_5_cout));
  FA fa_6 (.A(A5), .B(B5), .Cin(fa_5_cout), .S(S5), .Cout(fa_6_cout));
  FA fa_7 (.A(A6), .B(B6), .Cin(fa_6_cout), .S(S6), .Cout(fa_7_cout));
  FA fa_8 (.A(A7), .B(B7), .Cin(fa_7_cout), .S(S7), .Cout(fa_8_cout));
endmodule

module adder4bit (
  input  A0,
  input  B0,
  input  A1,
  input  B1,
  input  A2,
  input  B2,
  input  A3,
  input  B3,
  output S0,
  output S1,
  output S2,
  output S3
);

  wire fa_1_cout, fa_2_cout, fa_3_cout, fa_4_cout;

  FA fa_1 (.A(A0), .B(B0), .Cin(1'b0), .S(S0), .Cout(fa_1_cout));
  FA fa_2 (.A(A1), .B(B1), .Cin(fa_1_cout), .S(S1), .Cout(fa_2_cout));
  FA fa_3 (.A(A2), .B(B2), .Cin(fa_2_cout), .S(S2), .Cout(fa_3_cout));
  FA fa_4 (.A(A3), .B(B3), .Cin(fa_3_cout), .S(S3), .Cout(fa_4_cout));
endmodule
