// Logisim project F3.7.1_SRlatch.circ as structural Verilog: 1 circuit, main circuit main
module main (
  input  R,
  input  S,
  output Q,
  output out_4
);

  nor nor_1 (Q, R, out_4);
  nor nor_2 (out_4, Q, S);
endmodule
