// Logisim project F3.7.2_NANDsrlatch.circ as structural Verilog: 1 circuit, main circuit main
module main (
  input  R,
  input  S,
  output Q,
  output out_4
);

  nand nand_1 (Q, R, out_4);
  nand nand_2 (out_4, Q, S);
endmodule
