// Logisim project F3.7.6_flipRDlatch.circ as structural Verilog: 1 circuit, main circuit main
module main (
  input  R,
  input  D,
  input  WE,
  output out_4,
  output Q
);

  wire and_1_out, and_2_out, and_3_out, not_1_out, not_2_out;

  not not_1 (not_1_out, R);
  and and_1 (and_1_out, not_1_out, D);
  not not_2 (not_2_out, and_1_out);
  and and_2 (and_2_out, and_1_out, WE);
  and and_3 (and_3_out, WE, not_2_out);
  nor nor_1 (out_4, and_2_out, Q);
  nor nor_2 (Q, out_4, and_3_out);
endmodule
