// Logisim project F3.7.7_DFF.circ as structural Verilog: 2 circuits, main circuit main
module main (
  input  D,
  output Q
);

  wire clk_out, dlatch_1_q, not_1_out;

  Clock clk (.out(clk_out));
  not not_1 (not_1_out, clk_out);
  Dlatch dlatch_1 (.D(D), .WE(not_1_out), .Q(dlatch_1_q));  // open: NQ
  Dlatch dlatch_2 (.D(dlatch_1_q), .WE(clk_out), .Q(Q));  // open: NQ
endmodule

module Dlatch (
  input  D,
  input  WE,
  output Q,
  output NQ
);

  wire and_1_out, and_2_out, not_1_out;

  not not_1 (not_1_out, D);
  and and_1 (and_1_out, D, WE);
  and and_2 (and_2_out, WE, not_1_out);
  nor nor_1 (NQ, and_1_out, Q);
  nor nor_2 (Q, NQ, and_2_out);
endmodule
