// Logisim project F3.7.9_flipRDFF.circ as structural Verilog: 3 circuits, main circuit main
module main (
);

  wire clock_1_out, dff_1_q, not_1_out;

  Clock clock_1 (.out(clock_1_out));
  Dff dff_1 (.D(not_1_out), .clk(clock_1_out), .Q(dff_1_q));  // open: R
  not not_1 (not_1_out, dff_1_q);
endmodule

module Dlatch (
  input  D,
  input  WE,
  output Q,
  output NQ
);

  wire and_1_out, and_2_out, not_1_out;

  not not_1 (not_1_out, D);
  and and_1 (and_1_out, D, WE);
  and and_2 (and_2_out, WE, not_1_out);
  nor nor_1 (NQ, and_1_out, Q);
  nor nor_2 (Q, NQ, and_2_out);
endmodule

module Dff (
  input  R,
  input  D,
  input  clk,
  output Q
);

  wire and_1_out, and_2_out, dlatch_1_q, not_1_out, not_2_out, or_1_out, or_2_out;

  not not_1 (not_1_out, clk);
  not not_2 (not_2_out, R);
  or or_1 (or_1_out, not_1_out, R);
  and and_1 (and_1_out, not_2_out, D);
  Dlatch dlatch_1 (.D(and_1_out), .WE(or_1_out), .Q(dlatch_1_q));  // open: NQ
  or or_2 (or_2_out, clk, R);
  and and_2 (and_2_out, not_2_out, dlatch_1_q);
  Dlatch dlatch_2 (.D(and_2_out), .WE(or_2_out), .Q(Q));  // open: NQ
endmodule
