// Logisim project F5.1.1_IF.circ as structural Verilog: 1 circuit, main circuit main
module main (
  input  [3:0] in_1,
  output [7:0] out_2
);

  Multiplexer #(.select(4), .width(8)) multiplexer_1 (
    .in0(8'h8a), .in1(8'h90), .in2(8'ha0), .in3(8'hb1), .in4(8'h17), .in5(8'h29), .in6(8'hd1), .in7(8'hdf),
    .out(out_2), .sel(in_1));  // open: in8, in9, in10, in11, in12, in13, in14, in15

  // Other names for the same wires on the sheet: PC[3:0] = in_1
endmodule
