// Logisim project F5.1.2_GPR.circ as structural Verilog: 1 circuit, main circuit main
module main (
  input  [3:0] in_1,
  input  [7:0] in_2,
  input  EN,
  input  [1:0] in_4,
  output [7:0] out_5
);

  wire add, and_1_out, and_2_out, and_3_out, and_4_out, bner0, CLK, decoder_2_out0, decoder_2_out1,
       decoder_2_out2, decoder_2_out3, li;
  wire [3:0] PC;
  wire [7:0] and_5_out, and_6_out, and_7_out, and_8_out, bit_extender_1_out, bit_extender_2_out,
       bit_extender_3_out, bit_extender_4_out, GPR00_q, GPR01_q, GPR10_q, GPR11_q, multiplexer_1_out;

  Register #(.width(4)) u_PC (.D(in_1), .en(1'b1), .clk(CLK), .Q(PC));  // open: clr
  Multiplexer #(.select(4), .width(8)) multiplexer_1 (
    .in0(8'h8a), .in1(8'h90), .in2(8'ha0), .in3(8'hb1), .in4(8'h17), .in5(8'h29), .in6(8'hd1), .in7(8'hdf),
    .out(multiplexer_1_out), .sel(PC));  // open: in8, in9, in10, in11, in12, in13, in14, in15
  Clock clock_1 (.out(CLK));
  Decoder #(.enable("false"), .select(2)) decoder_1 (
    .out0(add), .out2(li), .out3(bner0), .sel(multiplexer_1_out[7:6]));  // open: out1
  Decoder #(.enable("false"), .select(2)) decoder_2 (
    .out0(decoder_2_out0), .out1(decoder_2_out1), .out2(decoder_2_out2), .out3(decoder_2_out3), .sel(in_4));
  assign bit_extender_1_out = {{7{decoder_2_out0}}, decoder_2_out0};  // Bit_Extender bit_extender_1
  assign bit_extender_2_out = {{7{decoder_2_out1}}, decoder_2_out1};  // Bit_Extender bit_extender_2
  assign bit_extender_3_out = {{7{decoder_2_out2}}, decoder_2_out2};  // Bit_Extender bit_extender_3
  assign bit_extender_4_out = {{7{decoder_2_out3}}, decoder_2_out3};  // Bit_Extender bit_extender_4
  and and_1 (and_1_out, decoder_2_out0, EN);
  and and_2 (and_2_out, decoder_2_out1, EN);
  and and_3 (and_3_out, decoder_2_out2, EN);
  and and_4 (and_4_out, decoder_2_out3, EN);
  Register GPR00 (.D(in_2), .en(and_1_out), .clk(CLK), .Q(GPR00_q));  // open: clr
  Register GPR01 (.D(in_2), .en(and_2_out), .clk(CLK), .Q(GPR01_q));  // open: clr
  Register GPR10 (.D(in_2), .en(and_3_out), .clk(CLK), .Q(GPR10_q));  // open: clr
  Register GPR11 (.D(in_2), .en(and_4_out), .clk(CLK), .Q(GPR11_q));  // open: clr
  assign and_5_out = bit_extender_1_out & GPR00_q;  // AND_Gate and_5, 8 bits wide
  assign and_6_out = bit_extender_2_out & GPR01_q;  // AND_Gate and_6, 8 bits wide
  assign and_7_out = bit_extender_3_out & GPR10_q;  // AND_Gate and_7, 8 bits wide
  assign and_8_out = bit_extender_4_out & GPR11_q;  // AND_Gate and_8, 8 bits wide
  assign out_5 = and_5_out | and_6_out | and_7_out | and_8_out;  // OR_Gate or_1, 8 bits wide
endmodule
