// Logisim project F5.2.1_add.sCPU.circ as structural Verilog: 1 circuit, main circuit main
module main (
);

  wire add, and_4_out, and_5_out, and_6_out, and_7_out, bner0, clk, decoder_2_out0, decoder_2_out1,
       decoder_2_out2, decoder_2_out3, decoder_3_out0, decoder_3_out1, decoder_3_out2, decoder_3_out3,
       decoder_4_out0, decoder_4_out1, decoder_4_out2, decoder_4_out3, li, wen;
  wire [1:0] raddr1, raddr1add, raddr2, raddr2add, waddr, waddradd, waddrli;
  wire [3:0] adder_2_out, and_1_out, PC;
  wire [5:0] bit_extender_2_out, bit_extender_3_out, data;
  wire [7:0] adder_1_out, and_8_out, and_9_out, and_10_out, and_11_out, and_12_out, and_13_out, and_14_out,
       and_15_out, bit_extender_1_out, bit_extender_5_out, bit_extender_6_out, bit_extender_7_out,
       bit_extender_8_out, bit_extender_9_out, bit_extender_10_out, bit_extender_11_out, bit_extender_12_out,
       GPR00_q, GPR01_q, GPR10_q, GPR11_q, rdata1, rdata2, wdata, wdataadd, wdatali;
  wire [7:6] multiplexer_1_out;

  assign bit_extender_1_out = {{7{add}}, add};  // Bit_Extender bit_extender_1
  assign bit_extender_2_out = {{5{add}}, add};  // Bit_Extender bit_extender_2
  Decoder #(.enable("false"), .select(2)) decoder_1 (
    .out0(add), .out2(li), .out3(bner0), .sel(multiplexer_1_out));  // open: out1
  Multiplexer #(.select(4), .width(8)) multiplexer_1 (
    .in0(8'h8a), .in1(8'h90), .in2(8'ha0), .in3(8'hb1), .in4(8'h17), .in5(8'h29), .in6(8'hd1), .in7(8'hdf),
    .in8(8'h40), .in9(8'h40), .in10(8'h40), .in11(8'h40), .in12(8'h40), .in13(8'h40), .in14(8'h40),
    .in15(8'h40), .out({multiplexer_1_out, data}), .sel(PC));
  assign bit_extender_3_out = {{5{li}}, li};  // Bit_Extender bit_extender_3
  assign {waddrli, and_1_out} = bit_extender_3_out & data;  // AND_Gate and_1, 6 bits wide
  assign {waddradd, raddr1add, raddr2add} = bit_extender_2_out & data;  // AND_Gate and_2, 6 bits wide
  assign wdatali = {{4{1'b0}}, and_1_out};  // Bit_Extender bit_extender_4
  assign wdataadd = bit_extender_1_out & adder_1_out;  // AND_Gate and_3, 8 bits wide
  Adder adder_1 (.a(rdata1), .b(rdata2), .out(adder_1_out));  // open: cin, cout
  or or_1 (wen, add, li);
  assign wdata = wdatali | wdataadd;  // OR_Gate or_2, 8 bits wide
  assign waddr = waddrli | waddradd;  // OR_Gate or_3, 2 bits wide
  assign raddr1 = raddr1add;  // OR_Gate or_4, 2 bits wide OR_Gate
  assign raddr2 = raddr2add;  // OR_Gate or_5, 2 bits wide OR_Gate
  Clock clock_1 (.out(clk));
  Decoder #(.enable("false"), .select(2)) decoder_2 (
    .out0(decoder_2_out0), .out1(decoder_2_out1), .out2(decoder_2_out2), .out3(decoder_2_out3), .sel(raddr2));
  Decoder #(.enable("false"), .select(2)) decoder_3 (
    .out0(decoder_3_out0), .out1(decoder_3_out1), .out2(decoder_3_out2), .out3(decoder_3_out3), .sel(raddr1));
  assign bit_extender_5_out = {{7{decoder_2_out0}}, decoder_2_out0};  // Bit_Extender bit_extender_5
  assign bit_extender_6_out = {{7{decoder_2_out1}}, decoder_2_out1};  // Bit_Extender bit_extender_6
  assign bit_extender_7_out = {{7{decoder_2_out2}}, decoder_2_out2};  // Bit_Extender bit_extender_7
  assign bit_extender_8_out = {{7{decoder_2_out3}}, decoder_2_out3};  // Bit_Extender bit_extender_8
  Decoder #(.enable("false"), .select(2)) decoder_4 (
    .out0(decoder_4_out0), .out1(decoder_4_out1), .out2(decoder_4_out2), .out3(decoder_4_out3), .sel(waddr));
  assign bit_extender_9_out = {{7{decoder_3_out0}}, decoder_3_out0};  // Bit_Extender bit_extender_9
  assign bit_extender_10_out = {{7{decoder_3_out1}}, decoder_3_out1};  // Bit_Extender bit_extender_10
  assign bit_extender_11_out = {{7{decoder_3_out2}}, decoder_3_out2};  // Bit_Extender bit_extender_11
  assign bit_extender_12_out = {{7{decoder_3_out3}}, decoder_3_out3};  // Bit_Extender bit_extender_12
  and and_4 (and_4_out, decoder_4_out0, wen);
  and and_5 (and_5_out, decoder_4_out1, wen);
  and and_6 (and_6_out, decoder_4_out2, wen);
  and and_7 (and_7_out, decoder_4_out3, wen);
  Register #(.width(4)) u_PC (.D(adder_2_out), .en(1'b1), .clk(clk), .Q(PC));  // open: clr
  Register GPR00 (.D(wdata), .en(and_4_out), .clk(clk), .Q(GPR00_q));  // open: clr
  Register GPR01 (.D(wdata), .en(and_5_out), .clk(clk), .Q(GPR01_q));  // open: clr
  Register GPR10 (.D(wdata), .en(and_6_out), .clk(clk), .Q(GPR10_q));  // open: clr
  Register GPR11 (.D(wdata), .en(and_7_out), .clk(clk), .Q(GPR11_q));  // open: clr
  assign and_8_out = GPR00_q & bit_extender_9_out;  // AND_Gate and_8, 8 bits wide
  assign and_9_out = GPR00_q & bit_extender_5_out;  // AND_Gate and_9, 8 bits wide
  assign and_10_out = GPR01_q & bit_extender_10_out;  // AND_Gate and_10, 8 bits wide
  assign and_11_out = GPR01_q & bit_extender_6_out;  // AND_Gate and_11, 8 bits wide
  assign and_12_out = GPR10_q & bit_extender_11_out;  // AND_Gate and_12, 8 bits wide
  assign and_13_out = GPR10_q & bit_extender_7_out;  // AND_Gate and_13, 8 bits wide
  assign and_14_out = GPR11_q & bit_extender_12_out;  // AND_Gate and_14, 8 bits wide
  assign and_15_out = GPR11_q & bit_extender_8_out;  // AND_Gate and_15, 8 bits wide
  Adder #(.width(4)) adder_2 (.a(4'b0001), .b(PC), .out(adder_2_out));  // open: cin, cout
  assign rdata1 = and_8_out | and_10_out | and_12_out | and_14_out;  // OR_Gate or_6, 8 bits wide
  assign rdata2 = and_9_out | and_11_out | and_13_out | and_15_out;  // OR_Gate or_7, 8 bits wide
endmodule
