// Logisim project F5.3.1_SumOddUpTo10.circ as structural Verilog: 1 circuit, main circuit main
module main (
);

  wire add, and_5_out, and_8_out, and_9_out, and_10_out, and_11_out, bner0, clk, comparator_1_eq,
       comparator_1_gt, comparator_1_lt, decoder_2_out0, decoder_2_out1, decoder_2_out2, decoder_2_out3,
       decoder_3_out0, decoder_3_out1, decoder_3_out2, decoder_3_out3, decoder_4_out0, decoder_4_out1,
       decoder_4_out2, decoder_4_out3, li, not_1_out, or_6_out, or_7_out, wen;
  wire [1:0] raddr1, raddr1add, raddr2, raddr2add, raddr2bner0, waddr, waddradd, waddrli;
  wire [3:0] adder_2_out, and_1_out, and_6_out, and_7_out, bit_extender_6_out, bit_extender_11_out, Branch,
       or_8_out, PC;
  wire [5:0] bit_extender_2_out, bit_extender_3_out, bit_extender_4_out, data;
  wire [7:0] adder_1_out, and_12_out, and_13_out, and_14_out, and_15_out, and_16_out, and_17_out, and_18_out,
       and_19_out, bit_extender_1_out, bit_extender_7_out, bit_extender_8_out, bit_extender_9_out,
       bit_extender_10_out, bit_extender_12_out, bit_extender_13_out, bit_extender_14_out,
       bit_extender_15_out, GPR00_q, GPR01_q, GPR10_q, GPR11_q, rdata1, rdata2, wdata, wdataadd, wdatali;
  wire [7:6] multiplexer_1_out;

  assign bit_extender_1_out = {{7{add}}, add};  // Bit_Extender bit_extender_1
  assign bit_extender_2_out = {{5{add}}, add};  // Bit_Extender bit_extender_2
  assign bit_extender_3_out = {{5{bner0}}, bner0};  // Bit_Extender bit_extender_3
  Multiplexer #(.select(4), .width(8)) multiplexer_1 (
    .in0(8'h8b), .in1(8'h91), .in2(8'ha0), .in3(8'hb2), .in4(8'h29), .in5(8'h17), .in6(8'hd1), .in7(8'hdf),
    .in8(8'h40), .in9(8'h40), .in10(8'h40), .in11(8'h40), .in12(8'h40), .in13(8'h40), .in14(8'h40),
    .in15(8'h40), .out({multiplexer_1_out, data}), .sel(PC));
  assign bit_extender_4_out = {{5{li}}, li};  // Bit_Extender bit_extender_4
  assign {waddrli, and_1_out} = bit_extender_4_out & data;  // AND_Gate and_1, 6 bits wide
  assign {waddradd, raddr1add, raddr2add} = bit_extender_2_out & data;  // AND_Gate and_2, 6 bits wide
  assign {Branch, raddr2bner0} = bit_extender_3_out & data;  // AND_Gate and_3, 6 bits wide
  Decoder #(.enable("false"), .select(2)) decoder_1 (
    .out0(add), .out2(li), .out3(bner0), .sel(multiplexer_1_out));  // open: out1
  assign wdatali = {{4{1'b0}}, and_1_out};  // Bit_Extender bit_extender_5
  assign wdataadd = bit_extender_1_out & adder_1_out;  // AND_Gate and_4, 8 bits wide
  Adder adder_1 (.a(rdata1), .b(rdata2), .out(adder_1_out));  // open: cin, cout
  or or_1 (wen, add, li);
  assign wdata = wdatali | wdataadd;  // OR_Gate or_2, 8 bits wide
  assign waddr = waddrli | waddradd;  // OR_Gate or_3, 2 bits wide
  assign raddr1 = raddr1add;  // OR_Gate or_4, 2 bits wide OR_Gate
  assign raddr2 = raddr2add | raddr2bner0;  // OR_Gate or_5, 2 bits wide
  Clock clock_1 (.out(clk));
  Comparator comparator_1 (.a(rdata1), .b(rdata2), .gt(comparator_1_gt), .eq(comparator_1_eq), .lt(comparator_1_lt));
  not not_1 (not_1_out, bner0);
  or or_6 (or_6_out, comparator_1_gt, comparator_1_lt);
  or or_7 (or_7_out, comparator_1_eq, not_1_out);
  Decoder #(.enable("false"), .select(2)) decoder_2 (
    .out0(decoder_2_out0), .out1(decoder_2_out1), .out2(decoder_2_out2), .out3(decoder_2_out3), .sel(raddr2));
  and and_5 (and_5_out, bner0, or_6_out);
  assign bit_extender_6_out = {{3{or_7_out}}, or_7_out};  // Bit_Extender bit_extender_6
  Decoder #(.enable("false"), .select(2)) decoder_3 (
    .out0(decoder_3_out0), .out1(decoder_3_out1), .out2(decoder_3_out2), .out3(decoder_3_out3), .sel(raddr1));
  assign bit_extender_7_out = {{7{decoder_2_out0}}, decoder_2_out0};  // Bit_Extender bit_extender_7
  assign bit_extender_8_out = {{7{decoder_2_out1}}, decoder_2_out1};  // Bit_Extender bit_extender_8
  assign bit_extender_9_out = {{7{decoder_2_out2}}, decoder_2_out2};  // Bit_Extender bit_extender_9
  assign bit_extender_10_out = {{7{decoder_2_out3}}, decoder_2_out3};  // Bit_Extender bit_extender_10
  assign bit_extender_11_out = {{3{and_5_out}}, and_5_out};  // Bit_Extender bit_extender_11
  assign and_6_out = bit_extender_11_out & Branch;  // AND_Gate and_6, 4 bits wide
  Decoder #(.enable("false"), .select(2)) decoder_4 (
    .out0(decoder_4_out0), .out1(decoder_4_out1), .out2(decoder_4_out2), .out3(decoder_4_out3), .sel(waddr));
  assign bit_extender_12_out = {{7{decoder_3_out0}}, decoder_3_out0};  // Bit_Extender bit_extender_12
  assign bit_extender_13_out = {{7{decoder_3_out1}}, decoder_3_out1};  // Bit_Extender bit_extender_13
  assign bit_extender_14_out = {{7{decoder_3_out2}}, decoder_3_out2};  // Bit_Extender bit_extender_14
  assign bit_extender_15_out = {{7{decoder_3_out3}}, decoder_3_out3};  // Bit_Extender bit_extender_15
  assign and_7_out = bit_extender_6_out & adder_2_out;  // AND_Gate and_7, 4 bits wide
  Register #(.width(4)) u_PC (.D(or_8_out), .en(1'b1), .clk(clk), .Q(PC));  // open: clr
  assign or_8_out = and_6_out | and_7_out;  // OR_Gate or_8, 4 bits wide
  Register GPR00 (.D(wdata), .en(and_8_out), .clk(clk), .Q(GPR00_q));  // open: clr
  and and_8 (and_8_out, decoder_4_out0, wen);
  Register GPR01 (.D(wdata), .en(and_9_out), .clk(clk), .Q(GPR01_q));  // open: clr
  and and_9 (and_9_out, decoder_4_out1, wen);
  Register GPR10 (.D(wdata), .en(and_10_out), .clk(clk), .Q(GPR10_q));  // open: clr
  and and_10 (and_10_out, decoder_4_out2, wen);
  Register GPR11 (.D(wdata), .en(and_11_out), .clk(clk), .Q(GPR11_q));  // open: clr
  and and_11 (and_11_out, decoder_4_out3, wen);
  assign and_12_out = GPR00_q & bit_extender_12_out;  // AND_Gate and_12, 8 bits wide
  assign and_13_out = GPR00_q & bit_extender_7_out;  // AND_Gate and_13, 8 bits wide
  assign and_14_out = GPR01_q & bit_extender_13_out;  // AND_Gate and_14, 8 bits wide
  assign and_15_out = GPR01_q & bit_extender_8_out;  // AND_Gate and_15, 8 bits wide
  assign and_16_out = GPR10_q & bit_extender_14_out;  // AND_Gate and_16, 8 bits wide
  assign and_17_out = GPR10_q & bit_extender_9_out;  // AND_Gate and_17, 8 bits wide
  assign and_18_out = GPR11_q & bit_extender_15_out;  // AND_Gate and_18, 8 bits wide
  assign and_19_out = GPR11_q & bit_extender_10_out;  // AND_Gate and_19, 8 bits wide
  Adder #(.width(4)) adder_2 (.a(4'b0001), .b(PC), .out(adder_2_out));  // open: cin, cout
  assign rdata1 = and_12_out | and_14_out | and_16_out | and_18_out;  // OR_Gate or_9, 8 bits wide
  assign rdata2 = and_13_out | and_15_out | and_17_out | and_19_out;  // OR_Gate or_10, 8 bits wide
endmodule
