// Logisim project F6.1.2_Led.circ as structural Verilog: 1 circuit, main circuit main
module main (
);

  wire add, and_1_out, and_2_out, and_3_out, and_4_out, and_5_out, bner0, clk, comparator_1_eq,
       decoder_2_out0, decoder_2_out1, decoder_2_out2, decoder_2_out3, decoder_3_out0, decoder_3_out1,
       decoder_3_out2, decoder_3_out3, decoder_4_out0, decoder_4_out1, decoder_4_out2, decoder_4_out3,
       decoder_5_out0, decoder_5_out2, decoder_5_out4, decoder_5_out6, li, not_1_out, outrs, wen;
  wire [1:0] raddr1, raddr1add, raddr1out, raddr2, raddr2add, raddr2bner0, raddrli, waddr, waddradd;
  wire [3:0] and_14_out, and_16_out, offset;
  wire [5:0] bit_extender_11_out, bit_extender_12_out, bit_extender_13_out, bit_extender_14_out, data;
  wire [7:0] adder_1_out, adder_2_out, and_6_out, and_7_out, and_8_out, and_9_out, and_10_out, and_11_out,
       and_12_out, and_13_out, bit_extender_1_out, bit_extender_2_out, bit_extender_3_out,
       bit_extender_4_out, bit_extender_5_out, bit_extender_6_out, bit_extender_7_out, bit_extender_8_out,
       bit_extender_9_out, bit_extender_10_out, GPR00_q, GPR01_q, GPR10_q, GPR11_q, multiplexer_2_out, PC,
       rdata1, rdata2, wdata, wdataadd, wdatali;
  wire [7:6] multiplexer_1_out;

  Multiplexer #(.select(8), .width(8)) multiplexer_1 (
    .in0(8'h8a), .in1(8'h90), .in2(8'ha0), .in3(8'hb1), .in4(8'h17), .in5(8'h29), .in6(8'hd1), .in7(8'h60),
    .in8(8'he3), .out({multiplexer_1_out, data}), .sel(PC));  // open: in9, in10, in11, in12, in13, in14, in15, in16, in17, in18, in19, in20, in21, in22, in23, in24, in25, in26, in27, in28, in29, in30, in31, in32, in33, in34, in35, in36, in37, in38, in39, in40, in41, in42, in43, in44, in45, in46, in47, in48, in49, in50, in51, in52, in53, in54, in55, in56, in57, in58, in59, in60, in61, in62, in63, in64, in65, in66, in67, in68, in69, in70, in71, in72, in73, in74, in75, in76, in77, in78, in79, in80, in81, in82, in83, in84, in85, in86, in87, in88, in89, in90, in91, in92, in93, in94, in95, in96, in97, in98, in99, in100, in101, in102, in103, in104, in105, in106, in107, in108, in109, in110, in111, in112, in113, in114, in115, in116, in117, in118, in119, in120, in121, in122, in123, in124, in125, in126, in127, in128, in129, in130, in131, in132, in133, in134, in135, in136, in137, in138, in139, in140, in141, in142, in143, in144, in145, in146, in147, in148, in149, in150, in151, in152, in153, in154, in155, in156, in157, in158, in159, in160, in161, in162, in163, in164, in165, in166, in167, in168, in169, in170, in171, in172, in173, in174, in175, in176, in177, in178, in179, in180, in181, in182, in183, in184, in185, in186, in187, in188, in189, in190, in191, in192, in193, in194, in195, in196, in197, in198, in199, in200, in201, in202, in203, in204, in205, in206, in207, in208, in209, in210, in211, in212, in213, in214, in215, in216, in217, in218, in219, in220, in221, in222, in223, in224, in225, in226, in227, in228, in229, in230, in231, in232, in233, in234, in235, in236, in237, in238, in239, in240, in241, in242, in243, in244, in245, in246, in247, in248, in249, in250, in251, in252, in253, in254, in255
  Decoder #(.enable("false"), .select(2)) decoder_1 (
    .out0(add), .out1(outrs), .out2(li), .out3(bner0), .sel(multiplexer_1_out));
  Decoder #(.enable("false"), .select(2)) decoder_2 (
    .out0(decoder_2_out0), .out1(decoder_2_out1), .out2(decoder_2_out2), .out3(decoder_2_out3), .sel(raddr2));
  Clock clock_1 (.out(clk));
  not not_1 (not_1_out, comparator_1_eq);
  Comparator #(.mode("unsigned")) comparator_1 (.a(rdata1), .b(rdata2), .eq(comparator_1_eq));  // open: gt, lt
  assign bit_extender_1_out = {{4{offset[3]}}, offset};  // Bit_Extender bit_extender_1
  and and_1 (and_1_out, not_1_out, bner0);
  Decoder #(.enable("false"), .select(2)) decoder_3 (
    .out0(decoder_3_out0), .out1(decoder_3_out1), .out2(decoder_3_out2), .out3(decoder_3_out3), .sel(raddr1));
  assign bit_extender_2_out = {{7{decoder_2_out0}}, decoder_2_out0};  // Bit_Extender bit_extender_2
  assign bit_extender_3_out = {{7{decoder_2_out1}}, decoder_2_out1};  // Bit_Extender bit_extender_3
  assign bit_extender_4_out = {{7{decoder_2_out2}}, decoder_2_out2};  // Bit_Extender bit_extender_4
  assign bit_extender_5_out = {{7{decoder_2_out3}}, decoder_2_out3};  // Bit_Extender bit_extender_5
  Multiplexer #(.width(8)) multiplexer_2 (
    .in0(8'h1), .in1(bit_extender_1_out), .out(multiplexer_2_out), .sel(and_1_out));
  Adder adder_1 (.a(multiplexer_2_out), .b(PC), .out(adder_1_out));  // open: cin, cout
  Decoder #(.enable("false"), .select(2)) decoder_4 (
    .out0(decoder_4_out0), .out1(decoder_4_out1), .out2(decoder_4_out2), .out3(decoder_4_out3), .sel(waddr));
  assign bit_extender_6_out = {{7{decoder_3_out0}}, decoder_3_out0};  // Bit_Extender bit_extender_6
  assign bit_extender_7_out = {{7{decoder_3_out1}}, decoder_3_out1};  // Bit_Extender bit_extender_7
  assign bit_extender_8_out = {{7{decoder_3_out2}}, decoder_3_out2};  // Bit_Extender bit_extender_8
  assign bit_extender_9_out = {{7{decoder_3_out3}}, decoder_3_out3};  // Bit_Extender bit_extender_9
  Register u_PC (.D(adder_1_out), .en(1'b1), .clk(clk), .Q(PC));  // open: clr
  Register GPR00 (.D(wdata), .en(and_2_out), .clk(clk), .Q(GPR00_q));  // open: clr
  and and_2 (and_2_out, decoder_4_out0, wen);
  Register GPR01 (.D(wdata), .en(and_3_out), .clk(clk), .Q(GPR01_q));  // open: clr
  and and_3 (and_3_out, decoder_4_out1, wen);
  Register GPR10 (.D(wdata), .en(and_4_out), .clk(clk), .Q(GPR10_q));  // open: clr
  and and_4 (and_4_out, decoder_4_out2, wen);
  Register GPR11 (.D(wdata), .en(and_5_out), .clk(clk), .Q(GPR11_q));  // open: clr
  and and_5 (and_5_out, decoder_4_out3, wen);
  // LedBar #(.inputtype("row")) idx000: pin names not known
  assign and_6_out = GPR00_q & bit_extender_6_out;  // AND_Gate and_6, 8 bits wide
  assign and_7_out = GPR00_q & bit_extender_2_out;  // AND_Gate and_7, 8 bits wide
  assign and_8_out = GPR01_q & bit_extender_7_out;  // AND_Gate and_8, 8 bits wide
  assign and_9_out = GPR01_q & bit_extender_3_out;  // AND_Gate and_9, 8 bits wide
  assign and_10_out = GPR10_q & bit_extender_8_out;  // AND_Gate and_10, 8 bits wide
  assign and_11_out = GPR10_q & bit_extender_4_out;  // AND_Gate and_11, 8 bits wide
  assign and_12_out = GPR11_q & bit_extender_9_out;  // AND_Gate and_12, 8 bits wide
  assign and_13_out = GPR11_q & bit_extender_5_out;  // AND_Gate and_13, 8 bits wide
  assign rdata1 = and_6_out | and_8_out | and_10_out | and_12_out;  // OR_Gate or_1, 8 bits wide
  assign rdata2 = and_7_out | and_9_out | and_11_out | and_13_out;  // OR_Gate or_2, 8 bits wide
  assign bit_extender_10_out = {{7{add}}, add};  // Bit_Extender bit_extender_10
  assign bit_extender_11_out = {{5{add}}, add};  // Bit_Extender bit_extender_11
  assign bit_extender_12_out = {{5{outrs}}, outrs};  // Bit_Extender bit_extender_12
  assign bit_extender_13_out = {{5{li}}, li};  // Bit_Extender bit_extender_13
  assign {raddrli, and_14_out} = bit_extender_13_out & data;  // AND_Gate and_14, 6 bits wide
  assign bit_extender_14_out = {{5{bner0}}, bner0};  // Bit_Extender bit_extender_14
  Adder adder_2 (.a(rdata1), .b(rdata2), .out(adder_2_out));  // open: cin, cout
  assign {waddradd, raddr1add, raddr2add} = bit_extender_11_out & data;  // AND_Gate and_15, 6 bits wide
  assign {raddr1out, and_16_out} = bit_extender_12_out & data;  // AND_Gate and_16, 6 bits wide
  Decoder #(.enable("false"), .select(3)) decoder_5 (
    .out0(decoder_5_out0), .out2(decoder_5_out2), .out4(decoder_5_out4), .out6(decoder_5_out6),
    .sel({and_14_out[3:2], 1'b0}));  // open: out1, out3, out5, out7
  assign {offset, raddr2bner0} = bit_extender_14_out & data;  // AND_Gate and_17, 6 bits wide
  assign wdataadd = bit_extender_10_out & adder_2_out;  // AND_Gate and_18, 8 bits wide
  Multiplexer #(.width(2)) multiplexer_3 (
    .in0(rdata1[1:0]), .in1(and_14_out[1:0]), .out(wdatali[1:0]), .sel(decoder_5_out0));
  Multiplexer #(.width(2)) multiplexer_4 (
    .in0(rdata1[3:2]), .in1(and_14_out[1:0]), .out(wdatali[3:2]), .sel(decoder_5_out2));
  Multiplexer #(.width(2)) multiplexer_5 (
    .in0(rdata1[5:4]), .in1(and_14_out[1:0]), .out(wdatali[5:4]), .sel(decoder_5_out4));
  Multiplexer #(.width(2)) multiplexer_6 (
    .in0(rdata1[7:6]), .in1(and_14_out[1:0]), .out(wdatali[7:6]), .sel(decoder_5_out6));
  or or_3 (wen, add, li);
  assign wdata = wdatali | wdataadd;  // OR_Gate or_4, 8 bits wide
  assign waddr = raddrli | waddradd;  // OR_Gate or_5, 2 bits wide
  assign raddr1 = raddr1add | raddrli | raddr1out | 2'b00;  // OR_Gate or_6, 2 bits wide
  assign raddr2 = raddr2add | raddr2bner0;  // OR_Gate or_7, 2 bits wide

  // Other names for the same wires on the sheet: waddrli[1:0] = raddrli
endmodule
